# Fritzing sketch LD1117V33 (saved by Fritzing 0.9.4)
circuit board: 9.77424cm x 6.55033cm
breadboards: 1

parts:
  VCC1 = Battery block 9V
  U1 = V_REG_LD1117VXX [package=78xxl]
  C4 = Electrolytic Capacitor [capacitance=100µF package="200 mil [THT, electrolytic]"]
  C3 = Electrolytic Capacitor [capacitance=0.1µF package="200 mil [THT, electrolytic]"]
  LED2 = LED - 3mm [color="Red (633nm)" package="3 mm [THT]"]
  R1 = Resistor [tolerance=±5% resistance=220 package=THT]

nets:
  N1: VCC1.-, U1.GND, C4.-, C3.-, R1.Pin_1
  N2: VCC1.+, U1.IN, C3.+
  N3: U1.OUT, C4.+, LED2.anode
  N4: LED2.cathode, R1.Pin_0
