# Fritzing sketch ESP01-Basic (saved by Fritzing 0.9.4)
circuit board: 9.59712cm x 5.93395cm
breadboards: 1

parts:
  R3 = Resistor [tolerance=±5% resistance=220 package=THT]
  R2 = Resistor [tolerance=±5% resistance=220 package=THT]
  R4 = Resistor [tolerance=±5% resistance=220 package=THT]
  U1 = ESP8266 WiFi Module [part_number=ESP8266]
  Part1 = Arduino Uno (Rev3)

nets:
  GND: R3.Pin_0, U1.GND, Part1.GND
  N1: R3.Pin_1, R2.Pin_0
  N2: R2.Pin_1, R4.Pin_1, U1.RXD
  N3: R4.Pin_0, Part1.D7
  VCC: U1.VCC, U1.CH_PD, Part1.3V3
  N4: U1.TXD, Part1.D6_PWM

custom parts:
  ESP8266 WiFi Module: Generic WiFi Module based on the ESP8266 with onboard PCB antenna and UART communications
